// Logisim project img202212030827881.circ as structural Verilog: 6 circuits, main circuit 计时器
// 16
module \_4位递增计数器  (
  input  Clock,
  input  [3:0] D,
  input  Load,
  input  Enable,
  input  Reset,
  output [3:0] Q
);

  Hex_Digit_Display hex_digit_display_1 (.value(Q));  // open: dp

  // Notes on the sheet:
  //   输入引脚
  //   4位二进制（十六进制）同步置数、异步清零功能的同步递增计数器
  //   输出引脚
  //   请勿更改封装外观，否则无法完成测试
  //   监控区
endmodule

// 6
module \六进制计数器  (
  input  Clock,
  input  [3:0] D,
  input  Load,
  input  Enable,
  input  Reset,
  output Co,
  output [3:0] Q
);

  Hex_Digit_Display hex_digit_display_1 (.value(Q));  // open: dp

  // Notes on the sheet:
  //   输入引脚
  //   六进制计数器
  //   输出引脚
  //   请勿更改封装外观，否则无法完成测试
  //   监控区
endmodule

// 10
module \十进制计数器  (
  input  Clock,
  input  [3:0] D,
  input  Load,
  input  Enable,
  input  Reset,
  output Co,
  output [3:0] Q
);

  \_4位递增计数器  \u_4位递增计数器_1  ();  // open: Clock, Enable, Reset, Q, D, Load
  Hex_Digit_Display hex_digit_display_1 (.value(Q));  // open: dp

  // Notes on the sheet:
  //   输入引脚
  //   十进制计数器
  //   输出引脚
  //   请勿更改封装外观，否则无法完成测试
  //   监控区
endmodule

// 60
module \六十进制计数器  (
  input  Clock,
  input  [3:0] D1,
  input  Load,
  input  Enable,
  input  [3:0] D0,
  input  Reset,
  output Co,
  output [3:0] Q1,
  output [3:0] Q0
);

  \六进制计数器  \u_六进制计数器_1  ();  // open: Clock, D, Load, Enable, Reset, Co, Q
  \十进制计数器  \u_十进制计数器_1  ();  // open: Clock, Enable, Reset, Co, Q, Load, D
  Hex_Digit_Display hex_digit_display_1 (.value(Q1));  // open: dp
  Hex_Digit_Display hex_digit_display_2 (.value(Q0));  // open: dp

  // Notes on the sheet:
  //   输入引脚
  //   六十进制计数器
  //   输出引脚
  //   请勿更改封装外观，否则无法完成测试
  //   监控区
endmodule

// 24
module \二十四进制计数器  (
  input  Clock,
  input  [3:0] D1,
  input  Load,
  input  Enable,
  input  [3:0] D0,
  input  Reset,
  output Co,
  output [3:0] Q1,
  output [3:0] Q0
);

  \十进制计数器  \u_十进制计数器_1  ();  // open: Clock, Enable, Reset, Co, Q, Load, D
  \十进制计数器  \u_十进制计数器_2  ();  // open: Clock, Enable, Reset, Co, Q, Load, D
  Hex_Digit_Display hex_digit_display_1 (.value(Q1));  // open: dp
  Hex_Digit_Display hex_digit_display_2 (.value(Q0));  // open: dp

  // Notes on the sheet:
  //   输入引脚
  //   二十四进制计数器
  //   输出引脚
  //   请勿更改封装外观，否则无法完成测试
  //   监控区
endmodule

module \计时器  (
  input  Clock,
  input  Load,
  input  [3:0] Dh1,
  input  [3:0] Dh0,
  input  [3:0] Dm1,
  input  [3:0] Dm0,
  input  [3:0] Ds1,
  input  [3:0] Ds0,
  input  Enable,
  input  Reset,
  output [3:0] H1,
  output [3:0] H0,
  output [3:0] M1,
  output [3:0] M0,
  output [3:0] S1,
  output [3:0] S0
);

  Hex_Digit_Display hex_digit_display_1 (.value(H1));  // open: dp
  Hex_Digit_Display hex_digit_display_2 (.value(H0));  // open: dp
  Hex_Digit_Display hex_digit_display_3 (.value(M1));  // open: dp
  Hex_Digit_Display hex_digit_display_4 (.value(M0));  // open: dp
  Hex_Digit_Display hex_digit_display_5 (.value(S0));  // open: dp
  Hex_Digit_Display hex_digit_display_6 (.value(S1));  // open: dp

  // Notes on the sheet:
  //   二十四小时计时器
  //   :
  //   输入引脚
  //   :
  //   请勿更改封装外观，否则无法完成测试
  //   输出引脚
endmodule
